// Logisim project temperature_controller_v2.circ as structural Verilog: 2 circuits, main circuit last four bits of 8 bit
// ok
module last_four_bits_of_8_bit (
  input  [7:0] in_1,
  input  in_2,
  input  [7:0] Current_Room_Temp,
  input  [7:0] in_4,
  input  [8:0] in_5,
  input  [7:0] Input_Body_Temp,
  input  [7:0] Body_Optimum_Temp,
  input  in_8,
  input  [7:0] Tolerance,
  input  in_10,
  input  in_11,
  input  in_12,
  output [7:0] Final_Room_Temperature
);

  wire and_1_out, and_2_out, comparator_1_gt, comparator_2_gt, comparator_3_gt, comparator_4_gt, not_1_out,
       not_2_out, not_3_out;
  wire [0:0] binary_to_bcd_1_b4;
  wire [3:0] binary_to_bcd_1_b0;
  wire [7:0] multiplexer_2_out, multiplexer_3_out, multiplexer_4_out, multiplexer_6_out, subtractor_1_out,
       subtractor_2_out, subtractor_3_out;
  wire [8:0] adder_2_out;

  Comparator comparator_1 (.a(Input_Body_Temp), .b(Body_Optimum_Temp), .gt(comparator_1_gt));  // open: eq, lt
  Comparator comparator_2 (.a(multiplexer_2_out), .b(Tolerance), .gt(comparator_2_gt));  // open: eq, lt
  Hex_Digit_Display hex_digit_display_1 (.value({in_12, in_11, in_10, binary_to_bcd_1_b4[0]}));  // open: dp
  Hex_Digit_Display hex_digit_display_2 (.value(binary_to_bcd_1_b0));  // open: dp
  not not_1 (not_1_out, comparator_2_gt);
  Subtractor subtractor_1 (.a(Input_Body_Temp), .b(Body_Optimum_Temp), .out(subtractor_1_out));  // open: bin, bout
  not not_2 (not_2_out, comparator_1_gt);
  Multiplexer #(.width(8)) multiplexer_1 (
    .in0(Body_Optimum_Temp), .in1(Input_Body_Temp), .sel(comparator_1_gt));  // open: out, en
  not not_3 (not_3_out, not_2_out);
  Subtractor subtractor_2 (.a(Body_Optimum_Temp), .b(Input_Body_Temp), .out(subtractor_2_out));  // open: bin, bout
  and and_1 (and_1_out, not_2_out, comparator_2_gt);
  Subtractor subtractor_3 (.a(Current_Room_Temp), .b(subtractor_1_out), .out(subtractor_3_out));  // open: bin, bout
  Adder adder_1 (.a(Current_Room_Temp), .b(subtractor_2_out));  // open: out, cin, cout
  Multiplexer #(.width(8)) multiplexer_2 (
    .in0(subtractor_2_out), .in1(subtractor_1_out), .out(multiplexer_2_out), .sel(comparator_1_gt));  // open: en
  LED Heater (.in(and_1_out));
  LED Cooler (.in(and_2_out));
  Comparator comparator_3 (.a(multiplexer_2_out), .b(Current_Room_Temp), .gt(comparator_3_gt));  // open: eq, lt
  and and_2 (and_2_out, not_3_out, comparator_2_gt);
  Multiplexer #(.width(8)) multiplexer_3 (
    .in0(multiplexer_6_out), .in1(multiplexer_4_out), .out(multiplexer_3_out), .sel(not_2_out));  // open: en
  Multiplexer #(.width(8)) multiplexer_4 (
    .in0(subtractor_3_out), .in1(in_1), .out(multiplexer_4_out), .sel(comparator_3_gt));  // open: en
  Adder #(.width(9)) adder_2 (
    .a({in_2, Current_Room_Temp}), .b({in_8, multiplexer_2_out}), .out(adder_2_out), .cin(in_2));  // open: cout
  binary_to_bcd binary_to_bcd_1 (
    .A(multiplexer_2_out[3]), .B(multiplexer_2_out[2]), .C(multiplexer_2_out[1]), .D(multiplexer_2_out[0]),
    .B3(binary_to_bcd_1_b0[3]), .B2(binary_to_bcd_1_b0[2]), .B1(binary_to_bcd_1_b0[1]),
    .B0(binary_to_bcd_1_b0[0]), .B4(binary_to_bcd_1_b4[0]));
  LED led_1 (.in(not_1_out));
  Comparator #(.width(9)) comparator_4 (.a(adder_2_out), .b(in_5), .gt(comparator_4_gt));  // open: eq, lt
  Multiplexer #(.width(8)) multiplexer_5 (
    .in0(Current_Room_Temp), .out(Final_Room_Temperature), .sel(comparator_2_gt));  // open: in1, en
  Multiplexer #(.width(8)) multiplexer_6 (
    .in0(adder_2_out[7:0]), .in1(in_4), .out(multiplexer_6_out), .sel(comparator_4_gt));  // open: en

  // Notes on the sheet:
  //   Temperature DIfference
  //   8-bit comparator
  //   tolerance comparator
  //   Input BT - Optimum BT
  //   Input body > Optimum Body
  //   Optimum body > Input Body
  //   Heater Control
  //   Room temp - TempDifference
  //   Optimum BT - Input BT
  //   last four bits of 8 bit
  //   Room Temp + TempDifference
  //   Temp Difrerence To show
  //   Cooler Control
  //   Cooling Boundary Comparator
  //   converting 4 bits to BCD
  //   splitting first four bits
  //   Comfort
  //   Do we modify room temp or Do we leave it Unchanged
endmodule

module binary_to_bcd (
  input  A,
  input  B,
  input  C,
  input  D,
  output B3,
  output B2,
  output B1,
  output B0,
  output B4
);

  wire and_1_out, and_2_out, and_3_out, and_4_out, and_5_out, and_7_out, not_1_out, not_2_out, not_3_out,
       not_4_out;

  not not_1 (not_1_out, C);
  not not_2 (not_2_out, C);
  and and_1 (and_1_out, C, B);
  not not_3 (not_3_out, A);
  and and_2 (and_2_out, not_1_out, A, B);
  and and_3 (and_3_out, not_3_out, C);
  and and_4 (and_4_out, B, A);
  and and_5 (and_5_out, A, C);
  not not_4 (not_4_out, B);
  and and_6 (B3, A, not_2_out, not_4_out);
  and and_7 (and_7_out, not_3_out, B);
  or or_1 (B1, and_3_out, and_2_out);
  or or_2 (B4, and_4_out, and_5_out);
  or or_3 (B2, and_1_out, and_7_out);

  assign B0 = D;
endmodule
